// Logisim project CC3MC-Giovanni MIlan Circuito -4.circ as structural Verilog: 8 circuits, main circuit main
module main (
  input  [3:0] A,
  input  [3:0] B,
  input  [2:0] in_3,
  output out_4,
  output out_5,
  output [3:0] S
);

  wire decodificador3x8_1_s0, decodificador3x8_1_s1, decodificador3x8_1_s2, decodificador3x8_1_s4;
  wire [3:0] add_4_1_out_5, sub_4_1_out_5;

  Decodificador3x8 decodificador3x8_1 (
    .S0(decodificador3x8_1_s0), .S1(decodificador3x8_1_s1), .S2(decodificador3x8_1_s2),
    .S4(decodificador3x8_1_s4), .\Operação (in_3));  // open: S3, S5, S6, S7
  Buffer buffer_1 (.B(B), .in_2(decodificador3x8_1_s0), .out_3(S));
  ADD_4 add_4_1 (.A(A), .out_4(out_4), .B(B), .in_3(1'b0), .out_5(add_4_1_out_5));
  Buffer buffer_2 (.B(add_4_1_out_5), .in_2(decodificador3x8_1_s1), .out_3(S));
  SUB_4 sub_4_1 (.A(A), .out_4(out_5), .B(B), .in_3(1'b0), .out_5(sub_4_1_out_5));
  Buffer buffer_3 (.B(sub_4_1_out_5), .in_2(decodificador3x8_1_s2), .out_3(S));
  Buffer_controlado_invertido buffer_controlado_invertido_1 (.B(B), .in_2(decodificador3x8_1_s4), .out_3(S));
endmodule

module ADD_1 (
  input  A,
  input  B,
  input  Vem_1,
  output S,
  output Vai_1
);

  wire and_1_out, and_2_out, or_1_out, xor_1_out;

  xor xor_1 (xor_1_out, A, B);
  or or_1 (or_1_out, B, Vem_1);
  and and_1 (and_1_out, B, Vem_1);
  and and_2 (and_2_out, or_1_out, A);
  xor xor_2 (S, xor_1_out, Vem_1);
  or or_2 (Vai_1, and_2_out, and_1_out);
endmodule

module ADD_4 (
  input  [3:0] A,
  input  [3:0] B,
  input  in_3,
  output out_4,
  output [3:0] out_5
);

  wire add_1_2_vai_1, add_1_3_vai_1, add_1_4_vai_1;

  ADD_1 add_1_1 (.A(add_1_2_vai_1), .B(B[3]), .Vem_1(A[3]), .S(out_5[3]), .Vai_1(out_4));
  ADD_1 add_1_2 (.A(add_1_3_vai_1), .B(B[2]), .Vem_1(A[2]), .S(out_5[2]), .Vai_1(add_1_2_vai_1));
  ADD_1 add_1_3 (.A(add_1_4_vai_1), .B(B[1]), .Vem_1(A[1]), .S(out_5[1]), .Vai_1(add_1_3_vai_1));
  ADD_1 add_1_4 (.A(in_3), .B(B[0]), .Vem_1(A[0]), .S(out_5[0]), .Vai_1(add_1_4_vai_1));
endmodule

module SUB_4 (
  input  [3:0] B,
  input  [3:0] A,
  input  in_3,
  output out_4,
  output [3:0] out_5
);

  wire sub_1_2_vai_1, sub_1_3_vai_1, sub_1_4_vai_1;

  SUB_1 sub_1_1 (.A(A[3]), .B(B[3]), .Vem_1(sub_1_2_vai_1), .S(out_5[3]), .Vai_1(out_4));
  SUB_1 sub_1_2 (.A(A[2]), .B(B[2]), .Vem_1(sub_1_3_vai_1), .S(out_5[2]), .Vai_1(sub_1_2_vai_1));
  SUB_1 sub_1_3 (.A(A[1]), .B(B[1]), .Vem_1(sub_1_4_vai_1), .S(out_5[1]), .Vai_1(sub_1_3_vai_1));
  SUB_1 sub_1_4 (.A(B[0]), .B(A[0]), .Vem_1(in_3), .S(out_5[0]), .Vai_1(sub_1_4_vai_1));
endmodule

module SUB_1 (
  input  A,
  input  B,
  input  Vem_1,
  output S,
  output Vai_1
);

  wire and_1_out, and_2_out, or_1_out, xor_1_out;

  xor xor_1 (xor_1_out, A, B);
  or or_1 (or_1_out, B, Vem_1);
  and and_1 (and_1_out, B, Vem_1);
  and and_2 (and_2_out, or_1_out, ~A);  // AND_Gate
  xor xor_2 (S, xor_1_out, Vem_1);
  or or_2 (Vai_1, and_2_out, and_1_out);
endmodule

module Buffer (
  input  [3:0] B,
  input  in_2,
  output [3:0] out_3
);

  assign out_3[3] = in_2 ? B[3] : 1'bz;  // Controlled_Buffer controlled_buffer_1
  assign out_3[2] = in_2 ? B[2] : 1'bz;  // Controlled_Buffer controlled_buffer_2
  assign out_3[1] = in_2 ? B[1] : 1'bz;  // Controlled_Buffer controlled_buffer_3
  assign out_3[0] = in_2 ? B[0] : 1'bz;  // Controlled_Buffer controlled_buffer_4
endmodule

module Buffer_controlado_invertido (
  input  [3:0] B,
  input  in_2,
  output [3:0] out_3
);

  assign out_3[3] = in_2 ? ~B[3] : 1'bz;  // Controlled_Inverter controlled_inverter_1
  assign out_3[2] = in_2 ? ~B[2] : 1'bz;  // Controlled_Inverter controlled_inverter_2
  assign out_3[1] = in_2 ? ~B[1] : 1'bz;  // Controlled_Inverter controlled_inverter_3
  assign out_3[0] = in_2 ? ~B[0] : 1'bz;  // Controlled_Inverter controlled_inverter_4
endmodule

module Decodificador3x8 (
  input  [2:0] \Operação ,
  output S0,
  output S1,
  output S2,
  output S3,
  output S4,
  output S5,
  output S6,
  output S7
);

  wire not_1_out, not_2_out, not_3_out, not_4_out, not_5_out, not_6_out, not_7_out, not_8_out, not_9_out,
       not_10_out, not_11_out, not_12_out;

  not not_1 (not_1_out, \Operação [0]);
  not not_2 (not_2_out, \Operação [2]);
  not not_3 (not_3_out, \Operação [2]);
  not not_4 (not_4_out, \Operação [0]);
  not not_5 (not_5_out, \Operação [2]);
  not not_6 (not_6_out, \Operação [0]);
  not not_7 (not_7_out, \Operação [2]);
  not not_8 (not_8_out, \Operação [0]);
  not not_9 (not_9_out, \Operação [2]);
  not not_10 (not_10_out, \Operação [2]);
  not not_11 (not_11_out, \Operação [2]);
  not not_12 (not_12_out, \Operação [2]);
  and and_1 (S7, \Operação [0], \Operação [2], \Operação [2]);
  and and_2 (S0, not_1_out, not_2_out, not_3_out);
  and and_3 (S1, not_4_out, not_5_out, \Operação [2]);
  and and_4 (S2, not_6_out, \Operação [2], not_7_out);
  and and_5 (S3, not_8_out, \Operação [2], \Operação [2]);
  and and_6 (S4, \Operação [0], not_9_out, not_10_out);
  and and_7 (S5, \Operação [0], not_11_out, \Operação [2]);
  and and_8 (S6, \Operação [0], \Operação [2], not_12_out);

  assign \Operação [1] = \Operação [2];
endmodule
