// Logisim project CC3MC-Giovanni MIlan Circuito -6.circ as structural Verilog: 11 circuits, main circuit main
module main (
  input  [3:0] A,
  input  [3:0] B,
  input  [2:0] in_3,
  output [3:0] S
);

  wire decodificador3x8_1_s0, decodificador3x8_1_s1, decodificador3x8_1_s2, decodificador3x8_1_s4,
       decodificador3x8_1_s5;
  wire [3:0] add_4_1_out_5, rot_l_1_abcd_2, sub_4_1_out_5, undriven;

  Or_4Bits or_4bits_1 ();  // open: A, B, S
  Decodificador3x8 decodificador3x8_1 (
    .S0(decodificador3x8_1_s0), .S1(decodificador3x8_1_s1), .S2(decodificador3x8_1_s2),
    .S4(decodificador3x8_1_s4), .S5(decodificador3x8_1_s5), .\Operação (in_3));  // open: S3, S6, S7
  Buffer buffer_1 (.B(B), .in_2(decodificador3x8_1_s0), .out_3(S));
  ADD_4 add_4_1 (.A(A), .B(B), .in_3(1'b0), .out_5(add_4_1_out_5));  // open: out_4
  Buffer buffer_2 (.B(add_4_1_out_5), .in_2(decodificador3x8_1_s1), .out_3(S));
  SUB_4 sub_4_1 (.A(A), .B(B), .in_3(1'b0), .out_5(sub_4_1_out_5));  // open: out_4
  Buffer buffer_3 (.B(sub_4_1_out_5), .in_2(decodificador3x8_1_s2), .out_3(S));
  Buffer_controlado_invertido buffer_controlado_invertido_1 (.B(B), .in_2(decodificador3x8_1_s4), .out_3(S));
  Rot_L rot_l_1 (.abcd_2(rot_l_1_abcd_2), .ABCD(A), .XY(B[1:0]));
  Rot_L rot_l_2 ();  // open: abcd_2, ABCD, XY
  Buffer buffer_4 (.B(undriven));  // open: in_2, out_3
endmodule

module ADD_1 (
  input  A,
  input  B,
  input  Vem_1,
  output S,
  output Vai_1
);

  wire and_1_out, and_2_out, or_1_out, xor_1_out;

  xor xor_1 (xor_1_out, A, B);
  or or_1 (or_1_out, B, Vem_1);
  and and_1 (and_1_out, B, Vem_1);
  and and_2 (and_2_out, or_1_out, A);
  xor xor_2 (S, xor_1_out, Vem_1);
  or or_2 (Vai_1, and_2_out, and_1_out);
endmodule

module ADD_4 (
  input  [3:0] A,
  input  [3:0] B,
  input  in_3,
  output out_4,
  output [3:0] out_5
);

  wire add_1_2_vai_1, add_1_3_vai_1, add_1_4_vai_1;

  ADD_1 add_1_1 (.A(add_1_2_vai_1), .B(B[3]), .Vem_1(A[3]), .S(out_5[3]), .Vai_1(out_4));
  ADD_1 add_1_2 (.A(add_1_3_vai_1), .B(B[2]), .Vem_1(A[2]), .S(out_5[2]), .Vai_1(add_1_2_vai_1));
  ADD_1 add_1_3 (.A(add_1_4_vai_1), .B(B[1]), .Vem_1(A[1]), .S(out_5[1]), .Vai_1(add_1_3_vai_1));
  ADD_1 add_1_4 (.A(in_3), .B(B[0]), .Vem_1(A[0]), .S(out_5[0]), .Vai_1(add_1_4_vai_1));
endmodule

module SUB_4 (
  input  [3:0] B,
  input  [3:0] A,
  input  in_3,
  output out_4,
  output [3:0] out_5
);

  wire sub_1_2_vai_1, sub_1_3_vai_1, sub_1_4_vai_1;

  SUB_1 sub_1_1 (.A(A[3]), .B(B[3]), .Vem_1(sub_1_2_vai_1), .S(out_5[3]), .Vai_1(out_4));
  SUB_1 sub_1_2 (.A(A[2]), .B(B[2]), .Vem_1(sub_1_3_vai_1), .S(out_5[2]), .Vai_1(sub_1_2_vai_1));
  SUB_1 sub_1_3 (.A(A[1]), .B(B[1]), .Vem_1(sub_1_4_vai_1), .S(out_5[1]), .Vai_1(sub_1_3_vai_1));
  SUB_1 sub_1_4 (.A(B[0]), .B(A[0]), .Vem_1(in_3), .S(out_5[0]), .Vai_1(sub_1_4_vai_1));
endmodule

module SUB_1 (
  input  A,
  input  B,
  input  Vem_1,
  output S,
  output Vai_1
);

  wire and_1_out, and_2_out, or_1_out, xor_1_out;

  xor xor_1 (xor_1_out, A, B);
  or or_1 (or_1_out, B, Vem_1);
  and and_1 (and_1_out, B, Vem_1);
  and and_2 (and_2_out, or_1_out, ~A);  // AND_Gate
  xor xor_2 (S, xor_1_out, Vem_1);
  or or_2 (Vai_1, and_2_out, and_1_out);
endmodule

module Buffer (
  input  [3:0] B,
  input  in_2,
  output [3:0] out_3
);

  assign out_3[3] = in_2 ? B[3] : 1'bz;  // Controlled_Buffer controlled_buffer_1
  assign out_3[2] = in_2 ? B[2] : 1'bz;  // Controlled_Buffer controlled_buffer_2
  assign out_3[0] = in_2 ? B[0] : 1'bz;  // Controlled_Buffer controlled_buffer_3
  assign out_3[1] = in_2 ? B[1] : 1'bz;  // Controlled_Buffer controlled_buffer_4
endmodule

module Buffer_controlado_invertido (
  input  [3:0] B,
  input  in_2,
  output [3:0] out_3
);

  assign out_3[2] = in_2 ? ~B[2] : 1'bz;  // Controlled_Inverter controlled_inverter_1
  assign out_3[3] = in_2 ? ~B[3] : 1'bz;  // Controlled_Inverter controlled_inverter_2
  assign out_3[0] = in_2 ? ~B[0] : 1'bz;  // Controlled_Inverter controlled_inverter_3
  assign out_3[1] = in_2 ? ~B[1] : 1'bz;  // Controlled_Inverter controlled_inverter_4
endmodule

module Decodificador3x8 (
  input  [2:0] \Operação ,
  output S0,
  output S1,
  output S2,
  output S3,
  output S4,
  output S5,
  output S6,
  output S7
);

  wire not_1_out, not_2_out, not_3_out, not_4_out, not_5_out, not_6_out, not_7_out, not_8_out, not_9_out,
       not_10_out, not_11_out, not_12_out;

  not not_1 (not_1_out, \Operação [0]);
  not not_2 (not_2_out, \Operação [2]);
  not not_3 (not_3_out, \Operação [2]);
  not not_4 (not_4_out, \Operação [0]);
  not not_5 (not_5_out, \Operação [2]);
  not not_6 (not_6_out, \Operação [0]);
  not not_7 (not_7_out, \Operação [2]);
  not not_8 (not_8_out, \Operação [0]);
  not not_9 (not_9_out, \Operação [2]);
  not not_10 (not_10_out, \Operação [2]);
  not not_11 (not_11_out, \Operação [2]);
  not not_12 (not_12_out, \Operação [2]);
  and and_1 (S7, \Operação [0], \Operação [2], \Operação [2]);
  and and_2 (S0, not_1_out, not_2_out, not_3_out);
  and and_3 (S1, not_4_out, not_5_out, \Operação [2]);
  and and_4 (S2, not_6_out, \Operação [2], not_7_out);
  and and_5 (S3, not_8_out, \Operação [2], \Operação [2]);
  and and_6 (S4, \Operação [0], not_9_out, not_10_out);
  and and_7 (S5, \Operação [0], not_11_out, \Operação [2]);
  and and_8 (S6, \Operação [0], \Operação [2], not_12_out);

  assign \Operação [1] = \Operação [2];
endmodule

module Rot_L (
  input  [3:0] ABCD,
  input  [1:0] XY,
  output [3:0] abcd_2
);

  wire and_1_out, and_2_out, and_3_out, and_4_out, and_5_out, and_6_out, and_7_out, and_8_out, and_9_out;

  and and_1 (and_1_out, ~XY[1], ~XY[0], ABCD[3]);  // AND_Gate
  and and_2 (and_2_out, ~XY[1], XY[0], ABCD[2]);  // AND_Gate
  and and_3 (and_3_out, XY[1], ~XY[0], ABCD[1]);  // AND_Gate
  and and_4 (and_4_out, XY[1], XY[0], ABCD[0]);
  and and_5 (and_5_out, ~XY[1], ~XY[0], ABCD[2]);  // AND_Gate
  and and_6 (and_6_out, ~XY[1], XY[0], ABCD[1]);  // AND_Gate
  and and_7 (and_7_out, XY[1], ~XY[0], ABCD[0]);  // AND_Gate
  and and_8 (and_8_out, ~XY[1], ~XY[0], ABCD[1]);  // AND_Gate
  and and_9 (and_9_out, ~XY[1], XY[0], ABCD[0]);  // AND_Gate
  and and_10 (abcd_2[0], ~XY[1], ~XY[0], ABCD[0]);  // AND_Gate
  or or_1 (abcd_2[3], and_1_out, and_2_out, and_3_out, and_4_out);
  or or_2 (abcd_2[2], and_5_out, and_6_out, and_7_out);
  or or_3 (abcd_2[1], and_8_out, and_9_out);
endmodule

module Rot_R (
  input  [3:0] ABCD,
  input  [1:0] XY,
  output [3:0] abcd_2
);

  wire and_1_out, and_2_out, and_3_out, and_4_out, and_5_out, and_6_out, and_7_out, and_8_out, and_9_out;

  and and_1 (and_1_out, ~XY[1], ~XY[0], ABCD[0]);  // AND_Gate
  and and_2 (and_2_out, ~XY[1], XY[0], ABCD[1]);  // AND_Gate
  and and_3 (and_3_out, XY[1], ~XY[0], ABCD[2]);  // AND_Gate
  and and_4 (and_4_out, XY[1], XY[0], ABCD[3]);
  and and_5 (and_5_out, ~XY[1], ~XY[0], ABCD[1]);  // AND_Gate
  and and_6 (and_6_out, ~XY[1], XY[0], ABCD[2]);  // AND_Gate
  and and_7 (and_7_out, XY[1], ~XY[0], ABCD[3]);  // AND_Gate
  and and_8 (and_8_out, ~XY[1], ~XY[0], ABCD[2]);  // AND_Gate
  and and_9 (and_9_out, ~XY[1], XY[0], ABCD[3]);  // AND_Gate
  and and_10 (abcd_2[3], ~XY[1], ~XY[0], ABCD[3]);  // AND_Gate
  or or_1 (abcd_2[0], and_1_out, and_2_out, and_3_out, and_4_out);
  or or_2 (abcd_2[1], and_5_out, and_6_out, and_7_out);
  or or_3 (abcd_2[2], and_8_out, and_9_out);
endmodule

module Or_4Bits (
  input  [3:0] B,
  input  [3:0] A,
  output [3:0] S
);

  or or_1 (S[3], A[3], B[3]);
  or or_2 (S[2], A[2], B[2]);
  or or_3 (S[1], A[1], B[1]);
  or or_4 (S[0], A[0], B[0]);
endmodule
