// Logisim project CC3MC-Giovanni MIlan Circuito.circ as structural Verilog: 3 circuits, main circuit main
module main (
  input  [3:0] in_1,
  input  [3:0] in_2,
  input  in_3,
  input  in_4,
  input  in_5,
  input  in_6,
  output out_7,
  output out_8,
  output [3:0] out_9,
  output out_10
);

  // ADD_1 add_1_1: pin names not known; wires that end beside it: out_8, in_4, out_10, in_6, in_5
  ADD_4 add_4_1 (.A(in_1), .out_4(out_7), .B(in_2), .in_3(in_3), .out_5(out_9));
endmodule

module ADD_1 (
  input  A,
  input  B,
  input  Vem_1,
  output S,
  output Vai_1
);

  wire and_1_out, and_2_out, or_1_out, xor_1_out;

  xor xor_1 (xor_1_out, A, B);
  or or_1 (or_1_out, B, Vem_1);
  and and_1 (and_1_out, B, Vem_1);
  and and_2 (and_2_out, or_1_out, A);
  xor xor_2 (S, xor_1_out, Vem_1);
  or or_2 (Vai_1, and_2_out, and_1_out);
endmodule

module ADD_4 (
  input  [3:0] A,
  input  [3:0] B,
  input  in_3,
  output out_4,
  output [3:0] out_5
);

  wire add_1_2_vai_1, add_1_3_vai_1, add_1_4_vai_1;

  ADD_1 add_1_1 (.A(add_1_2_vai_1), .B(B[3]), .Vem_1(A[3]), .S(out_5[3]), .Vai_1(out_4));
  ADD_1 add_1_2 (.A(add_1_3_vai_1), .B(B[2]), .Vem_1(A[2]), .S(out_5[2]), .Vai_1(add_1_2_vai_1));
  ADD_1 add_1_3 (.A(add_1_4_vai_1), .B(B[1]), .Vem_1(A[1]), .S(out_5[1]), .Vai_1(add_1_3_vai_1));
  ADD_1 add_1_4 (.A(in_3), .B(B[0]), .Vem_1(A[0]), .S(out_5[0]), .Vai_1(add_1_4_vai_1));
endmodule
