// Logisim project GiovanniMIlanCâmaraPinto_CPU_RISC.circ as structural Verilog: 16 circuits, main circuit main
module main (
);

  wire alu_1_overflow, alu_1_zero, button_1_out, clock_1_out, d_ff_1_q, d_ff_2_q, not_1_out, not_2_out,
       uc_1_clk_ac, uc_1_clk_pc, uc_1_clk_ram, uc_1_clk_rl, \uc_1_direção , uc_1_e, uc_1_load, uc_1_r_w,
       uc_1_rst_pc;
  wire [2:0] \uc_1_operação ;
  wire [3:0] ac_1_q, alu_1_s, mux_1_out_4, PC_q, ram_1_data, \uc_1_b_endereços , uc_1_dados, uc_1_operando;
  wire [7:0] ir_1_q, rom_1_data;

  not not_1 (not_1_out, uc_1_load);
  Counter #(.width(4), .max('hf), .trigger("falling")) PC (
    .load(uc_1_load), .D(uc_1_dados), .count(not_1_out), .Q(PC_q), .clk(uc_1_clk_pc), .clr(uc_1_rst_pc));  // open: carry
  UC uc_1 (
    .\B_Endereços (\uc_1_b_endereços ), .Operando(uc_1_operando), .\Direção (\uc_1_direção ), .E(uc_1_e),
    .\Operação (\uc_1_operação ), .\INSTRUÇÃO (ir_1_q), .Clock(clock_1_out), .Reset(button_1_out),
    .Rst_PC(uc_1_rst_pc), .clk_Rl(uc_1_clk_rl), .clk_PC(uc_1_clk_pc), .clk_AC(uc_1_clk_ac),
    .clk_RAM(uc_1_clk_ram), .Zero(d_ff_2_q), .Overflow(d_ff_1_q), .Load(uc_1_load), .Dados(uc_1_dados),
    .R_W(uc_1_r_w));
  Clock clock_1 (.out(clock_1_out));
  ROM #(.addrWidth(4)) rom_1 (.addr(PC_q), .data(rom_1_data));  // open: sel
  // Probe on uc_1_clk_rl
  IR ir_1 (.Q(ir_1_q), .D(rom_1_data), .Clock(uc_1_clk_rl));
  Button button_1 (.out(button_1_out));
  MUX mux_1 (.E(uc_1_operando), .Controle(uc_1_e), .D(ram_1_data), .out_4(mux_1_out_4));
  // Probe on ac_1_q
  ALU alu_1 (
    .D(\uc_1_direção ), .A(ac_1_q), .B(mux_1_out_4), .in_4(\uc_1_operação ), .S(alu_1_s), .Zero(alu_1_zero),
    .Overflow(alu_1_overflow));
  AC ac_1 (.Q(ac_1_q), .D(alu_1_s), .Clock(uc_1_clk_ac));
  // Probe on mux_1_out_4
  RAM #(.addrWidth(4), .dataWidth(4)) ram_1 (
    .addr(\uc_1_b_endereços ), .data(ram_1_data), .clk(uc_1_clk_ram), .ld(uc_1_r_w));  // open: sel, clr
  not not_2 (not_2_out, uc_1_r_w);
  D_Flip_Flop d_ff_1 (.clk(uc_1_clk_ac), .D(alu_1_overflow), .Q(d_ff_1_q));  // open: Qn, preset, en, reset
  D_Flip_Flop d_ff_2 (.clk(uc_1_clk_ac), .D(alu_1_zero), .Q(d_ff_2_q));  // open: Qn, preset, en, reset
  Buffer buffer_1 (.B(ac_1_q), .in_2(not_2_out), .out_3(ram_1_data));

  // Notes on the sheet:
  //   contents of rom_1 (hex, n*v repeats v):
  //   0 f0 1 f1 10 31 d0 f2 11 f0 12 f1 e4
  //   reset
  //   MOV
  //   0
  //   000
  //   1
  //   000
  //   MOV
  //   ADD
  //   001
  //   2
  //   3
  //   001
  //   ADD
  //   010
  //   SUB
  //   4
  //   010
  //   SUB
  //   5
  //   6
  //   011
  //   OR
  //   7
  //   OR
  //   011
  //   NOT
  //   8
  //   100
  //   100
  //   NOT
  //   9
  //   101
  //   A
  //   SHF
  //   101
  //   B
  //   SHF
  //   JPZ
  //   C
  //   110
  //   110
  //   JPO
  //   D
  //   111
  //   GO
  //   E
  //   STR
  //   111
  //   F
  //   Instruction Set
  //   0
  //   AC <= X
  //   1
  //   AC <= M(X)
  //   0
  //   AC <= AC+X
  //   1
  //   AC <= AC+M(X)
  //   0
  //   AC <= AC-X
  //   1
  //   AC <= AC-M(X)
  //   0
  //   AC <= AC OR X
  //   1
  //   AC <= AC OR M(X)
  //   0
  //   AC <= NOT X
  //   1
  //   AC <= NOT M( X)
  //   0
  //   AC <= AC << Q
  //   1
  //   AC <= AC >> Q
  //   0
  //   PC <= X SE FLAG Z
  //   PC <= X SE FLAG O
  //   1
  //   PC <= X
  //   0
  //   M(X) <= AC 
  //   1
endmodule

module ADD_1 (
  input  A,
  input  B,
  input  Vem_1,
  output S,
  output Vai_1
);

  wire and_1_out, and_2_out, or_1_out, xor_1_out;

  xor xor_1 (xor_1_out, A, B);
  or or_1 (or_1_out, B, Vem_1);
  and and_1 (and_1_out, B, Vem_1);
  and and_2 (and_2_out, or_1_out, A);
  xor xor_2 (S, xor_1_out, Vem_1);
  or or_2 (Vai_1, and_2_out, and_1_out);
endmodule

module ADD_4 (
  input  [3:0] A,
  input  [3:0] B,
  input  in_3,
  output out_4,
  output [3:0] out_5
);

  wire add_1_2_vai_1, add_1_3_vai_1, add_1_4_vai_1;

  ADD_1 add_1_1 (.A(add_1_2_vai_1), .B(B[3]), .Vem_1(A[3]), .S(out_5[3]), .Vai_1(out_4));
  ADD_1 add_1_2 (.A(add_1_3_vai_1), .B(B[2]), .Vem_1(A[2]), .S(out_5[2]), .Vai_1(add_1_2_vai_1));
  ADD_1 add_1_3 (.A(add_1_4_vai_1), .B(B[1]), .Vem_1(A[1]), .S(out_5[1]), .Vai_1(add_1_3_vai_1));
  ADD_1 add_1_4 (.A(in_3), .B(B[0]), .Vem_1(A[0]), .S(out_5[0]), .Vai_1(add_1_4_vai_1));
endmodule

module SUB_4 (
  input  [3:0] B,
  input  [3:0] A,
  input  in_3,
  output out_4,
  output [3:0] out_5
);

  wire sub_1_2_vai_1, sub_1_3_vai_1, sub_1_4_vai_1;

  SUB_1 sub_1_1 (.A(A[3]), .B(B[3]), .Vem_1(sub_1_2_vai_1), .S(out_5[3]), .Vai_1(out_4));
  SUB_1 sub_1_2 (.A(A[2]), .B(B[2]), .Vem_1(sub_1_3_vai_1), .S(out_5[2]), .Vai_1(sub_1_2_vai_1));
  SUB_1 sub_1_3 (.A(A[1]), .B(B[1]), .Vem_1(sub_1_4_vai_1), .S(out_5[1]), .Vai_1(sub_1_3_vai_1));
  SUB_1 sub_1_4 (.A(B[0]), .B(A[0]), .Vem_1(in_3), .S(out_5[0]), .Vai_1(sub_1_4_vai_1));
endmodule

module SUB_1 (
  input  A,
  input  B,
  input  Vem_1,
  output S,
  output Vai_1
);

  wire and_1_out, and_2_out, or_1_out, xor_1_out;

  xor xor_1 (xor_1_out, A, B);
  or or_1 (or_1_out, B, Vem_1);
  and and_1 (and_1_out, B, Vem_1);
  and and_2 (and_2_out, or_1_out, ~A);  // AND_Gate
  xor xor_2 (S, xor_1_out, Vem_1);
  or or_2 (Vai_1, and_2_out, and_1_out);
endmodule

module Buffer (
  input  [3:0] B,
  input  in_2,
  output [3:0] out_3
);

  assign out_3[3] = in_2 ? B[3] : 1'bz;  // Controlled_Buffer controlled_buffer_1
  assign out_3[2] = in_2 ? B[2] : 1'bz;  // Controlled_Buffer controlled_buffer_2
  assign out_3[0] = in_2 ? B[0] : 1'bz;  // Controlled_Buffer controlled_buffer_3
  assign out_3[1] = in_2 ? B[1] : 1'bz;  // Controlled_Buffer controlled_buffer_4
endmodule

module Buffer_controlado_invertido (
  input  [3:0] B,
  input  in_2,
  output [3:0] out_3
);

  assign out_3[2] = in_2 ? ~B[2] : 1'bz;  // Controlled_Inverter controlled_inverter_1
  assign out_3[3] = in_2 ? ~B[3] : 1'bz;  // Controlled_Inverter controlled_inverter_2
  assign out_3[1] = in_2 ? ~B[1] : 1'bz;  // Controlled_Inverter controlled_inverter_3
  assign out_3[0] = in_2 ? ~B[0] : 1'bz;  // Controlled_Inverter controlled_inverter_4
endmodule

module Decodificador3x8 (
  input  [2:0] \Operação ,
  output S0,
  output S1,
  output S2,
  output S3,
  output S4,
  output S5,
  output S6,
  output S7
);

  wire not_1_out, not_2_out, not_3_out, not_4_out, not_5_out, not_6_out, not_7_out, not_8_out, not_9_out,
       not_10_out, not_11_out, not_12_out;

  not not_1 (not_1_out, \Operação [2]);
  not not_2 (not_2_out, \Operação [1]);
  not not_3 (not_3_out, \Operação [0]);
  not not_4 (not_4_out, \Operação [2]);
  not not_5 (not_5_out, \Operação [1]);
  not not_6 (not_6_out, \Operação [2]);
  not not_7 (not_7_out, \Operação [0]);
  not not_8 (not_8_out, \Operação [2]);
  not not_9 (not_9_out, \Operação [1]);
  not not_10 (not_10_out, \Operação [0]);
  not not_11 (not_11_out, \Operação [1]);
  not not_12 (not_12_out, \Operação [0]);
  and and_1 (S7, \Operação [2], \Operação [1], \Operação [0]);
  and and_2 (S0, not_1_out, not_2_out, not_3_out);
  and and_3 (S1, not_4_out, not_5_out, \Operação [0]);
  and and_4 (S2, not_6_out, \Operação [1], not_7_out);
  and and_5 (S3, not_8_out, \Operação [1], \Operação [0]);
  and and_6 (S4, \Operação [2], not_9_out, not_10_out);
  and and_7 (S5, \Operação [2], not_11_out, \Operação [0]);
  and and_8 (S6, \Operação [2], \Operação [1], not_12_out);
endmodule

module Rot_L (
  input  [3:0] ABCD,
  input  [1:0] XY,
  output [3:0] abcd_2
);

  wire and_1_out, and_2_out, and_3_out, and_4_out, and_5_out, and_6_out, and_7_out, and_8_out, and_9_out;

  and and_1 (and_1_out, ~XY[1], ~XY[0], ABCD[3]);  // AND_Gate
  and and_2 (and_2_out, ~XY[1], XY[0], ABCD[2]);  // AND_Gate
  and and_3 (and_3_out, XY[1], ~XY[0], ABCD[1]);  // AND_Gate
  and and_4 (and_4_out, XY[1], XY[0], ABCD[0]);
  and and_5 (and_5_out, ~XY[1], ~XY[0], ABCD[2]);  // AND_Gate
  and and_6 (and_6_out, ~XY[1], XY[0], ABCD[1]);  // AND_Gate
  and and_7 (and_7_out, XY[1], ~XY[0], ABCD[0]);  // AND_Gate
  and and_8 (and_8_out, ~XY[1], ~XY[0], ABCD[1]);  // AND_Gate
  and and_9 (and_9_out, ~XY[1], XY[0], ABCD[0]);  // AND_Gate
  and and_10 (abcd_2[0], ~XY[1], ~XY[0], ABCD[0]);  // AND_Gate
  or or_1 (abcd_2[3], and_1_out, and_2_out, and_3_out, and_4_out);
  or or_2 (abcd_2[2], and_5_out, and_6_out, and_7_out);
  or or_3 (abcd_2[1], and_8_out, and_9_out);
endmodule

module Rot_R (
  input  [3:0] ABCD,
  input  [1:0] XY,
  output [3:0] abcd_2
);

  wire and_1_out, and_2_out, and_3_out, and_4_out, and_5_out, and_6_out, and_7_out, and_8_out, and_9_out;

  and and_1 (and_1_out, ~XY[1], ~XY[0], ABCD[0]);  // AND_Gate
  and and_2 (and_2_out, ~XY[1], XY[0], ABCD[1]);  // AND_Gate
  and and_3 (and_3_out, XY[1], ~XY[0], ABCD[2]);  // AND_Gate
  and and_4 (and_4_out, XY[1], XY[0], ABCD[3]);
  and and_5 (and_5_out, ~XY[1], ~XY[0], ABCD[1]);  // AND_Gate
  and and_6 (and_6_out, ~XY[1], XY[0], ABCD[2]);  // AND_Gate
  and and_7 (and_7_out, XY[1], ~XY[0], ABCD[3]);  // AND_Gate
  and and_8 (and_8_out, ~XY[1], ~XY[0], ABCD[2]);  // AND_Gate
  and and_9 (and_9_out, ~XY[1], XY[0], ABCD[3]);  // AND_Gate
  and and_10 (abcd_2[3], ~XY[1], ~XY[0], ABCD[3]);  // AND_Gate
  or or_1 (abcd_2[0], and_1_out, and_2_out, and_3_out, and_4_out);
  or or_2 (abcd_2[1], and_5_out, and_6_out, and_7_out);
  or or_3 (abcd_2[2], and_8_out, and_9_out);
endmodule

module Or_4Bits (
  input  [3:0] B,
  input  [3:0] A,
  output [3:0] S
);

  or or_1 (S[3], A[3], B[3]);
  or or_2 (S[2], A[2], B[2]);
  or or_3 (S[0], A[0], B[0]);
  or or_4 (S[1], A[1], B[1]);
endmodule

module ALU (
  input  D,
  input  [3:0] A,
  input  [3:0] B,
  input  [2:0] in_4,
  output Overflow,
  output [3:0] S,
  output Zero
);

  wire add_4_1_out_4, and_1_out, and_2_out, decodificador3x8_1_s0, decodificador3x8_1_s1,
       decodificador3x8_1_s2, decodificador3x8_1_s3, decodificador3x8_1_s4, decodificador3x8_1_s5,
       decodificador3x8_1_s6, decodificador3x8_1_s7, not_1_out, sub_4_1_out_4;
  wire [3:0] add_4_1_out_5, buffer_5_out_3, or_4bits_1_s, rot_l_1_abcd_2, rot_r_1_abcd_2, sub_4_1_out_5;

  or or_1 (Overflow, and_1_out, and_2_out);
  and and_1 (and_1_out, add_4_1_out_4, decodificador3x8_1_s1);
  and and_2 (and_2_out, sub_4_1_out_4, decodificador3x8_1_s2);
  Decodificador3x8 decodificador3x8_1 (
    .S0(decodificador3x8_1_s0), .S1(decodificador3x8_1_s1), .S2(decodificador3x8_1_s2),
    .S3(decodificador3x8_1_s3), .S4(decodificador3x8_1_s4), .S5(decodificador3x8_1_s5),
    .S6(decodificador3x8_1_s6), .S7(decodificador3x8_1_s7), .\Operação (in_4));
  nor nor_1 (Zero, decodificador3x8_1_s7, decodificador3x8_1_s6, S[0], S[1], S[2], S[3]);
  Buffer buffer_1 (.B(B), .in_2(decodificador3x8_1_s0), .out_3(S));
  ADD_4 add_4_1 (.A(A), .out_4(add_4_1_out_4), .B(B), .in_3(1'b0), .out_5(add_4_1_out_5));
  SUB_4 sub_4_1 (.A(A), .out_4(sub_4_1_out_4), .B(B), .in_3(1'b0), .out_5(sub_4_1_out_5));
  Buffer buffer_2 (.B(add_4_1_out_5), .in_2(decodificador3x8_1_s1), .out_3(S));
  Buffer buffer_3 (.B(sub_4_1_out_5), .in_2(decodificador3x8_1_s2), .out_3(S));
  Or_4Bits or_4bits_1 (.A(A), .B(B), .S(or_4bits_1_s));
  Buffer buffer_4 (.B(or_4bits_1_s), .in_2(decodificador3x8_1_s3), .out_3(S));
  Buffer_controlado_invertido buffer_controlado_invertido_1 (.B(B), .in_2(decodificador3x8_1_s4), .out_3(S));
  not not_1 (not_1_out, D);
  Rot_R rot_r_1 (.abcd_2(rot_r_1_abcd_2), .ABCD(A), .XY(B[1:0]));
  Rot_L rot_l_1 (.abcd_2(rot_l_1_abcd_2), .ABCD(A), .XY(B[1:0]));
  Buffer buffer_5 (.B(rot_r_1_abcd_2), .in_2(D), .out_3(buffer_5_out_3));
  Buffer buffer_6 (.B(rot_l_1_abcd_2), .in_2(not_1_out), .out_3(buffer_5_out_3));
  Buffer buffer_7 (.B(buffer_5_out_3), .in_2(decodificador3x8_1_s5), .out_3(S));
endmodule

module AC (
  input  Clock,
  input  [3:0] D,
  output [3:0] Q
);

  D_Flip_Flop D3 (.clk(Clock), .D(D[3]), .Q(Q[3]));  // open: Qn, preset, en, reset
  D_Flip_Flop D2 (.clk(Clock), .D(D[2]), .Q(Q[2]));  // open: Qn, preset, en, reset
  D_Flip_Flop D1 (.clk(Clock), .D(D[1]), .Q(Q[1]));  // open: Qn, preset, en, reset
  D_Flip_Flop D0 (.clk(Clock), .D(D[0]), .Q(Q[0]));  // open: Qn, preset, en, reset
endmodule

module MUX (
  input  [3:0] E,
  input  [3:0] D,
  input  Controle,
  output [3:0] out_4
);

  wire not_1_out;

  not not_1 (not_1_out, Controle);
  Buffer buffer_1 (.B(E), .in_2(not_1_out), .out_3(out_4));
  Buffer buffer_2 (.B(D), .in_2(Controle), .out_3(out_4));
endmodule

module IR (
  input  Clock,
  input  [7:0] D,
  output [7:0] Q
);

  D_Flip_Flop #(.trigger("falling")) D3 (.clk(Clock), .D(D[7]), .Q(Q[7]));  // open: Qn, preset, en, reset
  D_Flip_Flop #(.trigger("falling")) D2 (.clk(Clock), .D(D[6]), .Q(Q[6]));  // open: Qn, preset, en, reset
  D_Flip_Flop #(.trigger("falling")) D1 (.clk(Clock), .D(D[5]), .Q(Q[5]));  // open: Qn, preset, en, reset
  D_Flip_Flop #(.trigger("falling")) D0 (.clk(Clock), .D(D[4]), .Q(Q[4]));  // open: Qn, preset, en, reset
  D_Flip_Flop #(.trigger("falling")) D3_2 (.clk(Clock), .D(D[3]), .Q(Q[3]));  // open: Qn, preset, en, reset
  D_Flip_Flop #(.trigger("falling")) D2_2 (.clk(Clock), .D(D[2]), .Q(Q[2]));  // open: Qn, preset, en, reset
  D_Flip_Flop #(.trigger("falling")) D1_2 (.clk(Clock), .D(D[1]), .Q(Q[1]));  // open: Qn, preset, en, reset
  D_Flip_Flop #(.trigger("falling")) D0_2 (.clk(Clock), .D(D[0]), .Q(Q[0]));  // open: Qn, preset, en, reset
endmodule

module UC (
  input  Clock,
  input  [7:0] \INSTRUÇÃO ,
  input  Reset,
  input  Zero,
  input  Overflow,
  output clk_Rl,
  output clk_AC,
  output clk_RAM,
  output Rst_PC,
  output [3:0] Dados,
  output clk_PC,
  output [3:0] \B_Endereços ,
  output [3:0] Operando,
  output \Direção ,
  output E,
  output [2:0] \Operação ,
  output R_W,
  output Load
);

  wire GoTo_out, JPO_out, JPZ_out, nand_1_out;
  wire [1:0] counter_1_q;

  and GoTo (GoTo_out, \INSTRUÇÃO [7], \INSTRUÇÃO [6], \INSTRUÇÃO [5], ~\INSTRUÇÃO [4], clk_PC);  // AND_Gate
  nand Storage (R_W, \INSTRUÇÃO [7], \INSTRUÇÃO [6], \INSTRUÇÃO [5], \INSTRUÇÃO [4], clk_AC);
  Counter #(.width(2), .max('h3)) counter_1 (.Q(counter_1_q), .clk(Clock), .clr(Reset));  // open: load, D, count, carry
  and JPO (JPO_out, \INSTRUÇÃO [7], \INSTRUÇÃO [6], ~\INSTRUÇÃO [5], \INSTRUÇÃO [4], clk_PC, Overflow);  // AND_Gate
  or or_1 (Load, GoTo_out, JPO_out, JPZ_out);
  and and_1 (clk_Rl, ~counter_1_q[0], ~counter_1_q[1]);  // AND_Gate
  and and_2 (clk_PC, counter_1_q[0], ~counter_1_q[1]);  // AND_Gate
  and and_3 (clk_AC, ~counter_1_q[0], counter_1_q[1]);  // AND_Gate
  and JPZ (JPZ_out, \INSTRUÇÃO [7], \INSTRUÇÃO [6], ~\INSTRUÇÃO [5], ~\INSTRUÇÃO [4], clk_PC, Zero);  // AND_Gate
  and and_4 (clk_RAM, counter_1_q[0], counter_1_q[1]);
  nand nand_1 (nand_1_out, \INSTRUÇÃO [7], ~\INSTRUÇÃO [6], \INSTRUÇÃO [5]);  // NAND_Gate
  and and_5 (E, \INSTRUÇÃO [4], nand_1_out);

  assign \B_Endereços  = \INSTRUÇÃO [3:0];
  assign Dados = \INSTRUÇÃO [3:0];
  assign \Direção  = \INSTRUÇÃO [4];
  assign Operando = \INSTRUÇÃO [3:0];
  assign \Operação  = \INSTRUÇÃO [7:5];
  assign Rst_PC = Reset;
endmodule
